// Logisim project ALU.circ as structural Verilog: 1 circuit, main circuit ALU
module ALU (
  input  [31:0] A,
  input  [31:0] B,
  input  [4:0] Shift,
  input  [3:0] Codop,
  input  CarryIn,
  output [31:0] S,
  output [3:0] Flags
);

  wire [31:0] AandB, AxorB, LSL, LSR;

  assign AandB = A & B;  // AND_Gate AandB, 32 bits wide
  assign AxorB = ~(A | B);  // NOR_Gate AxorB, 32 bits wide
  Shifter #(.width(32)) shifter_1 (.in(AxorB), .\dist (Shift), .out(LSL));
  Shifter #(.shift("lr"), .width(32)) shifter_2 (.in(AxorB), .\dist (Shift), .out(LSR));

  // Other names for the same wires on the sheet: S_t[4:0] = Shift

  // Notes on the sheet:
  //   Note: for ROR, C = N
  //   Note 2: assume that shift > 0 for LSL and LSR
endmodule
